// Logisim project csarch2_case study 2 (combined circuit).circ as structural Verilog: 1 circuit, main circuit main
module main (
  input  [7:0] A,
  input  [1:0] op_sel,
  input  [7:0] B,
  input  [7:0] d_ext,
  input  [7:0] d_in,
  input  [1:0] d0,
  input  ld_a,
  input  [1:0] d1,
  input  [7:0] d_in_2,
  input  load_bus_ext,
  input  ld_b,
  input  [7:0] d_in_3,
  input  ld_ir,
  output [7:0] opcode_out
);

  wire clk_out;
  wire [1:0] multiplexer_3_out;
  wire [7:0] adder_1_out, adder_2_out, multiplexer_1_out, subtractor_1_out, subtractor_2_out;

  Register register_1 (.D(d_in), .en(ld_a), .Q(A), .clk(clk_out));  // open: clr
  Register register_2 (.D(d_in), .en(ld_b), .Q(B), .clk(clk_out));  // open: clr
  Clock clk (.out(clk_out));
  Adder adder_1 (.a(A), .b(8'h1), .out(adder_1_out));  // open: cin, cout
  Subtractor subtractor_1 (.a(A), .b(8'h1), .out(subtractor_1_out));  // open: bin, bout
  Adder adder_2 (.a(B), .b(8'h1), .out(adder_2_out));  // open: cin, cout
  Subtractor subtractor_2 (.a(B), .b(8'h1), .out(subtractor_2_out));  // open: bin, bout
  Multiplexer #(.select(2), .width(8)) multiplexer_1 (
    .in0(adder_1_out), .in1(subtractor_1_out), .in2(adder_2_out), .in3(subtractor_2_out),
    .out(multiplexer_1_out), .sel(op_sel));  // open: en
  Register register_3 (.D(d_in), .en(ld_ir), .Q(opcode_out), .clk(clk_out));  // open: clr
  Multiplexer #(.select(2), .width(8)) multiplexer_2 (
    .in0(multiplexer_1_out), .in1(d_ext), .in2(A), .in3(B), .out(d_in), .sel(multiplexer_3_out));  // open: en
  Multiplexer #(.width(2)) multiplexer_3 (.in0(d0), .in1(d1), .out(multiplexer_3_out), .sel(load_bus_ext));  // open: en

  assign d_in_2 = d_in;
  assign d_in_3 = d_in;
endmodule
