// Logisim project csarch2_case study 2.circ as structural Verilog: 5 circuits, main circuit main
// Bus
module main (
  input  [7:0] external_data_in,
  input  [1:0] bus_sel,
  input  [1:0] ALU_Result,
  input  [1:0] External_Data,
  input  load_bus_ext,
  output [7:0] external_data_out
);

  wire clk_out, decoder_1_out0;
  wire [7:0] alu_1_alu_out, ir_1_opcode_out, rega_1_q_a_out;

  Clock clk (.out(clk_out));
  IR ir_1 (.clk(clk_out), .opcode_out(ir_1_opcode_out));  // open: d_in, ld_ir
  Decoder #(.select(2)) decoder_1 (
    .out0(decoder_1_out0), .out1(decoder_1_out0), .out2(decoder_1_out0));  // open: out3, sel, en
  ALU alu_1 (.B(rega_1_q_a_out), .alu_out(alu_1_alu_out));  // open: A, op_sel
  RegA rega_1 (.d_in(external_data_out), .ld_a(decoder_1_out0), .clk(clk_out), .q_a_out(rega_1_q_a_out));
  RegB regb_1 (.d_in(external_data_out), .ld_b(decoder_1_out0), .clk(clk_out), .q_b_out(rega_1_q_a_out));
  Multiplexer #(.select(2), .width(8)) multiplexer_1 (
    .in0(alu_1_alu_out), .in1(external_data_in), .in2(rega_1_q_a_out), .in3(rega_1_q_a_out),
    .out(external_data_out), .sel(bus_sel));  // open: en
  Multiplexer #(.width(2)) multiplexer_2 (
    .in0(ALU_Result), .in1(External_Data), .out(bus_sel), .sel(load_bus_ext));  // open: en
endmodule

module RegA (
  input  [7:0] d_in,
  input  ld_a,
  input  clk,
  output [7:0] q_a_out
);

  Register register_1 (.D(d_in), .en(ld_a), .Q(q_a_out), .clk(clk));  // open: clr
endmodule

module RegB (
  input  [7:0] d_in,
  input  ld_b,
  input  clk,
  output [7:0] q_b_out
);

  Register register_1 (.D(d_in), .en(ld_b), .Q(q_b_out), .clk(clk));  // open: clr
endmodule

module IR (
  input  [7:0] d_in,
  input  ld_ir,
  input  clk,
  output [7:0] opcode_out
);

  Register register_1 (.D(d_in), .en(ld_ir), .Q(opcode_out), .clk(clk));  // open: clr
endmodule

module ALU (
  input  [7:0] A,
  input  [1:0] op_sel,
  input  [7:0] B,
  output [7:0] alu_out
);

  wire [7:0] adder_1_out, adder_2_out, subtractor_1_out, subtractor_2_out, undriven, undriven_2;

  Adder adder_1 (.a(A), .b(8'h1), .out(adder_1_out));  // open: cin, cout
  Subtractor subtractor_1 (.a(undriven), .b(8'h1), .out(subtractor_1_out));  // open: bin, bout
  Adder adder_2 (.a(B), .b(8'h1), .out(adder_2_out));  // open: cin, cout
  Subtractor subtractor_2 (.a(undriven_2), .b(8'h1), .out(subtractor_2_out));  // open: bin, bout
  Multiplexer #(.select(2), .width(8)) multiplexer_1 (
    .in0(adder_1_out), .in1(subtractor_1_out), .in2(adder_2_out), .in3(subtractor_2_out), .out(alu_out),
    .sel(op_sel));  // open: en
endmodule
