// Logisim project csarch2_group7.circ as structural Verilog: 3 circuits, main circuit main
module main (
  input  [7:0] ir_in,
  input  [7:0] d_in,
  input  data_in,
  input  select_a,
  input  [7:0] d_in_2,
  input  data_in_2,
  input  select_b,
  output [7:0] OUTPUT_A,
  output [7:0] OUTPUT_B
);

  wire clk_out, not_1_out;
  wire [1:0] decoder_1_result;
  wire [7:0] alu_1_output, multiplexer_1_out, multiplexer_2_out, multiplexer_3_out;

  not not_1 (not_1_out, select_a);
  Multiplexer #(.width(8)) multiplexer_1 (
    .in0(alu_1_output), .in1(d_in), .out(multiplexer_1_out), .sel(data_in));  // open: en
  Multiplexer #(.width(8)) multiplexer_2 (
    .in0(alu_1_output), .in1(d_in_2), .out(multiplexer_2_out), .sel(data_in_2));  // open: en
  Multiplexer #(.width(8)) multiplexer_3 (
    .in0(OUTPUT_A), .in1(OUTPUT_B), .out(multiplexer_3_out), .sel(not_1_out));  // open: en
  Register A (.D(multiplexer_1_out), .en(select_a), .Q(OUTPUT_A), .clk(clk_out));  // open: clr
  Register B (.D(multiplexer_2_out), .en(select_b), .Q(OUTPUT_B), .clk(clk_out));  // open: clr
  ALU alu_1 (.\input (multiplexer_3_out), .operation(decoder_1_result), .\output (alu_1_output));
  Clock clk (.out(clk_out));
  Decoder decoder_1 (.ir_in(ir_in), .result(decoder_1_result));

  // Notes on the sheet:
  //   manual input for A
  //   manual input for B
  //   0000 0000 = INC A
  //   0000 0001 = DEC A
  //   0000 0010 = INC B
  //   0000 0011 = DEC A
  //   input opcode here
endmodule

module ALU (
  input  [7:0] \input ,
  input  [1:0] operation,
  output [7:0] \output 
);

  wire [7:0] adder_1_out, adder_2_out, subtractor_1_out, subtractor_2_out;

  Adder adder_1 (.a(\input ), .b(8'h1), .out(adder_1_out));  // open: cin, cout
  Subtractor subtractor_1 (.a(\input ), .b(8'h1), .out(subtractor_1_out));  // open: bin, bout
  Adder adder_2 (.a(\input ), .b(8'h1), .out(adder_2_out));  // open: cin, cout
  Subtractor subtractor_2 (.a(\input ), .b(8'h1), .out(subtractor_2_out));  // open: bin, bout
  Multiplexer #(.select(2), .width(8)) multiplexer_1 (
    .in0(adder_1_out), .in1(subtractor_1_out), .in2(adder_2_out), .in3(subtractor_2_out), .out(\output ),
    .sel(operation));  // open: en

  // Notes on the sheet:
  //   00
  //   01
  //   10
  //   11
endmodule

// opcode
module Decoder (
  input  [7:0] ir_in,
  output [1:0] result
);


  assign result = ir_in[1:0];

  // Notes on the sheet:
  //   input
endmodule
